// Logisim project superscalar_proc.circ as structural Verilog: 17 circuits, main circuit processor
module processor (
  input  in_1
);

  wire parse_instruction_1_double_const, scheduler_1_next, scheduler_1_superscalar;
  wire [1:0] parse_instruction_1_write_select_0, parse_instruction_1_write_select_1;
  wire [2:0] parse_instruction_1_operation_0, parse_instruction_1_operation_1;
  wire [3:0] registers_1_registers_2, registers_1_registers_3, registers_1_registers_4,
       registers_1_registers_5;
  wire [7:0] calc_1_value_2, calc_2_value_2, combine_1_value_0_2, combine_1_value_1_2,
       parse_instruction_1_value_0, parse_instruction_1_value_1, scheduler_1_command_0, scheduler_1_command_1;
  wire [15:0] registers_1_registers;
  wire [31:0] memory_1_block;

  // Probe on memory_1_block
  memory memory_1 (.Next(scheduler_1_next), .Clock(in_1), .Block(memory_1_block));
  // Probe on scheduler_1_superscalar
  // Probe on scheduler_1_next
  // Probe on scheduler_1_command_1
  // Probe on scheduler_1_command_0
  scheduler scheduler_1 (
    .Input_1(memory_1_block), .Clock(in_1), .Superscalar(scheduler_1_superscalar),
    .Command_0(scheduler_1_command_0), .Command_1(scheduler_1_command_1), .Next(scheduler_1_next));
  parse_instruction parse_instruction_1 (
    .Command_0(scheduler_1_command_0), .Command_1(scheduler_1_command_1),
    .Registers({registers_1_registers_5, registers_1_registers_4, registers_1_registers_3, registers_1_registers_2, registers_1_registers}),
    .Superscalar(scheduler_1_superscalar), .Value_0(parse_instruction_1_value_0),
    .Operation_0(parse_instruction_1_operation_0), .Write_Select_0(parse_instruction_1_write_select_0),
    .Value_1(parse_instruction_1_value_1), .Operation_1(parse_instruction_1_operation_1),
    .Write_Select_1(parse_instruction_1_write_select_1), .Double_Const(parse_instruction_1_double_const));
  // Probe on parse_instruction_1_write_select_0
  // Probe on parse_instruction_1_write_select_1
  calc calc_1 (
    .Value(parse_instruction_1_value_0),
    .Registers({registers_1_registers_5, registers_1_registers_4, registers_1_registers_3, registers_1_registers_2, registers_1_registers}),
    .Select(parse_instruction_1_write_select_0), .Operation(parse_instruction_1_operation_0),
    .Value_2(calc_1_value_2));
  // Probe on calc_1_value_2
  // Probe on calc_2_value_2
  calc calc_2 (
    .Value(parse_instruction_1_value_1),
    .Registers({registers_1_registers_5, registers_1_registers_4, registers_1_registers_3, registers_1_registers_2, registers_1_registers}),
    .Select(parse_instruction_1_write_select_1), .Operation(parse_instruction_1_operation_1),
    .Value_2(calc_2_value_2));
  combine combine_1 (
    .Value_0(calc_1_value_2), .Value_1(calc_2_value_2), .Double_Const(parse_instruction_1_double_const),
    .Value_0_2(combine_1_value_0_2), .Value_1_2(combine_1_value_1_2));
  registers registers_1 (
    .Input_1(combine_1_value_0_2), .Input_2(combine_1_value_1_2),
    .Select_1(parse_instruction_1_write_select_0), .Select_2(parse_instruction_1_write_select_1),
    .Double_Write(scheduler_1_superscalar), .Clock(in_1),
    .Registers({registers_1_registers_5, registers_1_registers_4, registers_1_registers_3, registers_1_registers_2, registers_1_registers}));
  Hex_Digit_Display hex_digit_display_1 (.value(registers_1_registers[7:4]));  // open: dp
  Hex_Digit_Display hex_digit_display_2 (.value(registers_1_registers[3:0]));  // open: dp
  Hex_Digit_Display hex_digit_display_3 (.value(registers_1_registers[15:12]));  // open: dp
  Hex_Digit_Display hex_digit_display_4 (.value(registers_1_registers[11:8]));  // open: dp
  Hex_Digit_Display hex_digit_display_5 (.value(registers_1_registers_3));  // open: dp
  Hex_Digit_Display hex_digit_display_6 (.value(registers_1_registers_2));  // open: dp
  Hex_Digit_Display hex_digit_display_7 (.value(registers_1_registers_5));  // open: dp
  Hex_Digit_Display hex_digit_display_8 (.value(registers_1_registers_4));  // open: dp

  // Notes on the sheet:
  //   Superscalar?
  //   Advance Memory
  //   Commands 
  //   Parse
  //   Registers to Write
  //   Value 1
  //   Value 2
  //   Combine Bits
  //   Registers
  //   Register 0
  //   Register 1
  //   Register 2
  //   Register 3
endmodule

module registers (
  input  [7:0] Input_1,
  input  [7:0] Input_2,
  input  [1:0] Select_1,
  input  [1:0] Select_2,
  input  Double_Write,
  input  Clock,
  output [31:0] Registers
);

  wire and_1_out, and_2_out, and_3_out, and_4_out, demultiplexer_1_out0, demultiplexer_1_out1,
       demultiplexer_1_out2, demultiplexer_1_out3, demultiplexer_2_out0, demultiplexer_2_out1,
       demultiplexer_2_out2, demultiplexer_2_out3, or_1_out, or_2_out, or_3_out, or_4_out;
  wire [7:0] multiplexer_1_out, multiplexer_2_out, multiplexer_3_out, multiplexer_4_out;

  Demultiplexer #(.select(2), .disabled(0), .enable("false")) demultiplexer_1 (
    .out0(demultiplexer_1_out0), .out1(demultiplexer_1_out1), .out2(demultiplexer_1_out2),
    .out3(demultiplexer_1_out3), .in(1'b1), .sel(Select_1));
  Demultiplexer #(.select(2), .disabled(0), .enable("false")) demultiplexer_2 (
    .out0(demultiplexer_2_out0), .out1(demultiplexer_2_out1), .out2(demultiplexer_2_out2),
    .out3(demultiplexer_2_out3), .in(1'b1), .sel(Select_2));
  and and_1 (and_1_out, demultiplexer_2_out3, Double_Write);
  // Probe on Input_2
  and and_2 (and_2_out, demultiplexer_2_out2, Double_Write);
  // Probe on Input_1
  Multiplexer #(.width(8), .enable("false")) multiplexer_1 (
    .in0(Input_2), .in1(Input_1), .out(multiplexer_1_out), .sel(demultiplexer_1_out0));
  Multiplexer #(.width(8), .enable("false")) multiplexer_2 (
    .in0(Input_2), .in1(Input_1), .out(multiplexer_2_out), .sel(demultiplexer_1_out1));
  Multiplexer #(.width(8), .enable("false")) multiplexer_3 (
    .in0(Input_2), .in1(Input_1), .out(multiplexer_3_out), .sel(demultiplexer_1_out2));
  Multiplexer #(.width(8), .enable("false")) multiplexer_4 (
    .in0(Input_2), .in1(Input_1), .out(multiplexer_4_out), .sel(demultiplexer_1_out3));
  and and_3 (and_3_out, demultiplexer_2_out1, Double_Write);
  and and_4 (and_4_out, demultiplexer_2_out0, Double_Write);
  or or_1 (or_1_out, demultiplexer_1_out0, and_4_out);
  or or_2 (or_2_out, demultiplexer_1_out1, and_3_out);
  or or_3 (or_3_out, demultiplexer_1_out2, and_2_out);
  or or_4 (or_4_out, demultiplexer_1_out3, and_1_out);
  Register #(.trigger("falling")) register_1 (
    .D(multiplexer_1_out), .en(or_1_out), .Q(Registers[7:0]), .clk(Clock));  // open: clr
  Register #(.trigger("falling")) register_2 (
    .D(multiplexer_2_out), .en(or_2_out), .Q(Registers[15:8]), .clk(Clock));  // open: clr
  Register #(.trigger("falling")) register_3 (
    .D(multiplexer_3_out), .en(or_3_out), .Q(Registers[23:16]), .clk(Clock));  // open: clr
  Register #(.trigger("falling")) register_4 (
    .D(multiplexer_4_out), .en(or_4_out), .Q(Registers[31:24]), .clk(Clock));  // open: clr
endmodule

// parse
module parse_instruction (
  input  [7:0] Command_0,
  input  [7:0] Command_1,
  input  [31:0] Registers,
  input  Superscalar,
  output [7:0] Value_0,
  output [2:0] Operation_0,
  output [1:0] Write_Select_0,
  output [7:0] Value_1,
  output [2:0] Operation_1,
  output [1:0] Write_Select_1,
  output Double_Const
);

  wire [2:0] decode_1_operation, decode_2_operation;

  decode decode_1 (
    .Command(Command_0), .Registers(Registers), .Value(Value_0), .Operation(decode_1_operation),
    .Write_Select(Write_Select_0));
  decode decode_2 (
    .Command(Command_1), .Registers(Registers), .Value(Value_1), .Operation(decode_2_operation),
    .Write_Select(Write_Select_1));
  // Probe on decode_1_operation
  double_check double_check_1 (
    .Operation_0(decode_1_operation), .Operation_1(decode_2_operation), .Superscalar(Superscalar),
    .Write_Registe_0(Write_Select_0), .Write_Registe_1(Write_Select_1), .Operation_0_2(Operation_0),
    .Operation_1_2(Operation_1), .Double_Const(Double_Const));
endmodule

// dec
module decode (
  input  [7:0] Command,
  input  [31:0] Registers,
  output [7:0] Value,
  output [2:0] Operation,
  output [1:0] Write_Select
);

  wire not_1_out;
  wire [2:0] multiplexer_2_out;
  wire [7:0] multiplexer_1_out, multiplexer_3_out;

  not not_1 (not_1_out, Command[7]);
  // Probe on Command[5:2]
  Multiplexer #(.select(2), .width(8), .enable("false")) multiplexer_1 (
    .in0(Registers[7:0]), .in1(Registers[15:8]), .in2(Registers[23:16]), .in3(Registers[31:24]),
    .out(multiplexer_1_out), .sel(Command[3:2]));
  Multiplexer #(.width(3), .enable("false")) multiplexer_2 (
    .in0(3'b000), .in1(3'b100), .out(multiplexer_2_out), .sel(Command[6]));
  Multiplexer #(.width(8), .enable("false")) multiplexer_3 (
    .in0({4'b0000, Command[5:2]}), .in1({Command[5:2], 4'b0000}), .out(multiplexer_3_out), .sel(Command[6]));
  Multiplexer #(.width(3), .enable("false")) multiplexer_4 (
    .in0(multiplexer_2_out), .in1(Command[6:4]), .out(Operation), .sel(not_1_out));
  Multiplexer #(.width(2), .enable("false")) multiplexer_5 (
    .in0(Command[1:0]), .in1(Command[1:0]), .out(Write_Select), .sel(not_1_out));
  Multiplexer #(.width(8), .enable("false")) multiplexer_6 (
    .in0(multiplexer_3_out), .in1(multiplexer_1_out), .out(Value), .sel(not_1_out));
endmodule

// double
module double_check (
  input  [2:0] Operation_0,
  input  [2:0] Operation_1,
  input  Superscalar,
  input  [1:0] Write_Registe_0,
  input  [1:0] Write_Registe_1,
  output [2:0] Operation_0_2,
  output [2:0] Operation_1_2,
  output Double_Const
);

  wire comparator_1_eq;

  Comparator #(.width(2)) comparator_1 (
    .a(Write_Registe_0), .b(Write_Registe_1), .eq(comparator_1_eq));  // open: gt, lt
  and and_1 (Double_Const, Superscalar, comparator_1_eq);
  Multiplexer #(.width(3), .enable("false")) multiplexer_1 (
    .in0(Operation_0), .in1({Operation_0[2:1], 1'b0}), .out(Operation_0_2), .sel(Double_Const));
  Multiplexer #(.width(3), .enable("false")) multiplexer_2 (
    .in0(Operation_1), .in1({Operation_1[2:1], 1'b0}), .out(Operation_1_2), .sel(Double_Const));
endmodule

module calc (
  input  [7:0] Value,
  input  [31:0] Registers,
  input  [1:0] Select,
  input  [2:0] Operation,
  output [7:0] Value_2
);

  wire [7:0] multiplexer_1_out;

  Multiplexer #(.select(2), .width(8), .enable("false")) multiplexer_1 (
    .in0(Registers[7:0]), .in1(Registers[15:8]), .in2(Registers[23:16]), .in3(Registers[31:24]),
    .out(multiplexer_1_out), .sel(Select));
  alu alu_1 (.Input_1(Value), .Input_2(multiplexer_1_out), .Select_1(Operation), .out_4(Value_2));
endmodule

module alu (
  input  [7:0] Input_1,
  input  [7:0] Input_2,
  input  [2:0] Select_1,
  output [7:0] out_4
);

  wire [7:0] adder_1_out, divider_1_out, multiplier_1_out, subtractor_1_out;

  Adder adder_1 (.a(Input_1), .b(Input_2), .out(adder_1_out));  // open: cin, cout
  Subtractor subtractor_1 (.a(Input_1), .b(Input_2), .out(subtractor_1_out));  // open: bin, bout
  Multiplier multiplier_1 (.a(Input_1), .b(Input_2), .out(multiplier_1_out));  // open: cin, cout
  Divider divider_1 (.a(Input_1), .b(Input_2), .out(divider_1_out));  // open: upper, rem
  Multiplexer #(.select(3), .width(8), .enable("false")) multiplexer_1 (
    .in0(Input_1), .in1(adder_1_out), .in2(subtractor_1_out), .in3(Input_1), .in4(multiplier_1_out),
    .in5(divider_1_out), .in6(Input_1), .in7(Input_1), .out(out_4), .sel(Select_1));
endmodule

module cons_check (
  input  [7:0] Command_1,
  input  [7:0] Command_2,
  output Success
);

  wire and_1_out, comparator_1_eq, xor_1_out;

  and and_1 (and_1_out, Command_1[7], Command_2[7]);
  xor xor_1 (xor_1_out, Command_1[6], Command_2[6]);
  Comparator #(.width(2), .mode("unsigned")) comparator_1 (
    .a(Command_1[1:0]), .b(Command_2[1:0]), .eq(comparator_1_eq));  // open: gt, lt
  and and_2 (Success, and_1_out, xor_1_out, comparator_1_eq);
endmodule

// sched
module scheduler (
  input  [31:0] Input_1,
  input  Clock,
  output Superscalar,
  output [7:0] Command_0,
  output [7:0] Command_1,
  output Next
);

  wire is_empty_1_empty, is_empty_2_empty;
  wire [31:0] find_sup_1_new_buffer_0, find_sup_1_new_buffer_1, multiplexer_1_out, multiplexer_2_out,
       register_1_q, register_2_q;

  // Probe on multiplexer_1_out
  Multiplexer #(.width(32), .enable("false")) multiplexer_1 (
    .in0(find_sup_1_new_buffer_1), .in1(Input_1), .out(multiplexer_1_out), .sel(Next));
  or or_1 (Next, is_empty_1_empty, is_empty_2_empty);
  is_empty is_empty_1 (.Old_Buffer(find_sup_1_new_buffer_1), .Empty(is_empty_1_empty));
  // Probe on register_1_q
  Register #(.width(32)) register_1 (.D(multiplexer_1_out), .en(1'b1), .Q(register_1_q), .clk(Clock));  // open: clr
  // Probe on multiplexer_2_out
  Multiplexer #(.width(32), .enable("false")) multiplexer_2 (
    .in0(find_sup_1_new_buffer_0), .in1(register_1_q), .out(multiplexer_2_out), .sel(is_empty_2_empty));
  is_empty is_empty_2 (.Old_Buffer(register_2_q), .Empty(is_empty_2_empty));
  // Probe on register_2_q
  Register #(.width(32)) register_2 (.D(multiplexer_2_out), .en(1'b1), .Q(register_2_q), .clk(Clock));  // open: clr
  // Probe on Command_0
  // Probe on Command_1
  find_sup find_sup_1 (
    .Old_Buffer_0(register_2_q), .Old_Buffer_1(register_1_q), .Command_0(Command_0), .Command_1(Command_1),
    .Superscalar(Superscalar), .New_Buffer_0(find_sup_1_new_buffer_0), .New_Buffer_1(find_sup_1_new_buffer_1));

  // Notes on the sheet:
  //   Next Buffer 1
  //   Buffer 1
  //   Next Buffer 0
  //   Buffer 0
  //   Commands
endmodule

// findsup
module find_sup (
  input  [31:0] Old_Buffer_0,
  input  [31:0] Old_Buffer_1,
  output [7:0] Command_0,
  output [7:0] Command_1,
  output Superscalar,
  output [31:0] New_Buffer_0,
  output [31:0] New_Buffer_1
);

  wire and_1_out, and_2_out, cons_check_1_success, dep_check_1_success, dep_check_2_success,
       dep_check_3_success, dep_check_4_success, dep_check_5_success, dep_check_6_success, or_1_out,
       raw_check_1_success, raw_check_2_success, raw_check_3_success;
  wire [1:0] multiplexer_1_out, multiplexer_2_out, multiplexer_3_out;
  wire [7:0] multiplexer_4_out, multiplexer_5_out;

  cons_check cons_check_1 (
    .Command_1(Old_Buffer_0[7:0]), .Command_2(Old_Buffer_0[15:8]), .Success(cons_check_1_success));
  dep_check dep_check_1 (.Command_1(Old_Buffer_0[7:0]), .Command_2(Old_Buffer_0[15:8]), .Success(dep_check_1_success));
  or or_1 (or_1_out, dep_check_1_success, cons_check_1_success);
  dep_check dep_check_2 (.Command_1(Old_Buffer_0[7:0]), .Command_2(Old_Buffer_0[23:16]), .Success(dep_check_2_success));
  dep_check dep_check_3 (
    .Command_1(Old_Buffer_0[23:16]), .Command_2(Old_Buffer_0[15:8]), .Success(dep_check_3_success));
  and and_1 (and_1_out, dep_check_2_success, dep_check_3_success, raw_check_1_success);
  dep_check dep_check_4 (
    .Command_1(Old_Buffer_0[31:24]), .Command_2(Old_Buffer_0[15:8]), .Success(dep_check_4_success));
  dep_check dep_check_5 (.Command_1(Old_Buffer_0[7:0]), .Command_2(Old_Buffer_0[31:24]), .Success(dep_check_5_success));
  RAW_check raw_check_1 (
    .Command_1(Old_Buffer_0[15:8]), .Command_2(Old_Buffer_0[23:16]), .Success(raw_check_1_success));
  dep_check dep_check_6 (
    .Command_1(Old_Buffer_0[31:24]), .Command_2(Old_Buffer_0[23:16]), .Success(dep_check_6_success));
  RAW_check raw_check_2 (
    .Command_1(Old_Buffer_0[15:8]), .Command_2(Old_Buffer_0[31:24]), .Success(raw_check_2_success));
  and and_2 (and_2_out, dep_check_5_success, dep_check_4_success, raw_check_2_success, dep_check_6_success, raw_check_3_success);
  RAW_check raw_check_3 (
    .Command_1(Old_Buffer_0[23:16]), .Command_2(Old_Buffer_0[31:24]), .Success(raw_check_3_success));
  Multiplexer #(.width(2), .enable("false")) multiplexer_1 (
    .in0(2'b00), .in1(2'b11), .out(multiplexer_1_out), .sel(and_2_out));
  Multiplexer #(.width(2), .enable("false")) multiplexer_2 (
    .in0(multiplexer_1_out), .in1(2'b10), .out(multiplexer_2_out), .sel(and_1_out));
  Multiplexer #(.width(2), .enable("false")) multiplexer_3 (
    .in0(multiplexer_2_out), .in1(2'b01), .out(multiplexer_3_out), .sel(or_1_out));
  Multiplexer #(.width(8), .enable("false")) multiplexer_4 (
    .in0({8{1'b0}}), .in1(Old_Buffer_0[31:24]), .out(multiplexer_4_out), .sel(and_2_out));
  Multiplexer #(.width(8), .enable("false")) multiplexer_5 (
    .in0(multiplexer_4_out), .in1(Old_Buffer_0[23:16]), .out(multiplexer_5_out), .sel(and_1_out));
  Multiplexer #(.width(8), .enable("false")) multiplexer_6 (
    .in0(multiplexer_5_out), .in1(Old_Buffer_0[15:8]), .out(Command_1), .sel(or_1_out));
  advance advance_1 (
    .Old_Buffer_0(Old_Buffer_0), .Old_Buffer_1(Old_Buffer_1), .Superscalar(multiplexer_3_out),
    .New_Buffer_0(New_Buffer_0), .New_Buffer_1(New_Buffer_1));
  or or_2 (Superscalar, multiplexer_3_out[0], multiplexer_3_out[1]);

  assign Command_0 = Old_Buffer_0[7:0];
endmodule

module dep_check (
  input  [7:0] Command_1,
  input  [7:0] Command_2,
  output Success
);

  wire raw_check_1_success, waw_check_1_success;

  RAW_check raw_check_1 (.Command_1(Command_1), .Command_2(Command_2), .Success(raw_check_1_success));
  WAW_check waw_check_1 (.Command_1(Command_1), .Command_2(Command_2), .Success(waw_check_1_success));
  and and_1 (Success, raw_check_1_success, waw_check_1_success);
endmodule

// wAW
module WAW_check (
  input  [7:0] Command_1,
  input  [7:0] Command_2,
  output Success
);

  wire comparator_1_eq;

  Comparator #(.width(2), .mode("unsigned")) comparator_1 (
    .a(Command_1[1:0]), .b(Command_2[1:0]), .eq(comparator_1_eq));  // open: gt, lt
  not not_1 (Success, comparator_1_eq);
endmodule

// RAW
module RAW_check (
  input  [7:0] Command_1,
  input  [7:0] Command_2,
  output Success
);

  wire comparator_1_eq, not_1_out;

  not not_1 (not_1_out, comparator_1_eq);
  Comparator #(.width(2), .mode("unsigned")) comparator_1 (
    .a(Command_1[1:0]), .b(Command_2[3:2]), .eq(comparator_1_eq));  // open: gt, lt
  or or_1 (Success, not_1_out, Command_2[7]);
endmodule

module advance (
  input  [31:0] Old_Buffer_0,
  input  [31:0] Old_Buffer_1,
  input  [1:0] Superscalar,
  output [31:0] New_Buffer_0,
  output [31:0] New_Buffer_1
);

  Multiplexer #(.select(2), .width(32), .enable("false")) multiplexer_1 (
    .in0({Old_Buffer_1[7:0], Old_Buffer_0[31:8]}), .in1({Old_Buffer_1[15:0], Old_Buffer_0[31:16]}),
    .in2({Old_Buffer_1[15:0], Old_Buffer_0[31:24], Old_Buffer_0[15:8]}),
    .in3({Old_Buffer_1[15:0], Old_Buffer_0[23:8]}), .out(New_Buffer_0), .sel(Superscalar));
  Multiplexer #(.select(2), .width(32), .enable("false")) multiplexer_2 (
    .in0({{8{1'b0}}, Old_Buffer_1[31:8]}), .in1({{16{1'b0}}, Old_Buffer_1[31:16]}),
    .in2({{16{1'b0}}, Old_Buffer_1[31:16]}), .in3({{16{1'b0}}, Old_Buffer_1[31:16]}), .out(New_Buffer_1),
    .sel(Superscalar));
endmodule

// empty
module is_empty (
  input  [31:0] Old_Buffer,
  output Empty
);

  Comparator #(.width(32)) comparator_1 (.a(Old_Buffer), .b({32{1'b0}}), .eq(Empty));  // open: gt, lt
endmodule

// mem
module memory (
  input  Next,
  input  Clock,
  output [31:0] Block
);

  wire [7:0] adder_1_out, register_1_q;

  Register register_1 (.D(adder_1_out), .en(Next), .Q(register_1_q), .clk(Clock));  // open: clr
  ROM #(.dataWidth(32)) rom_1 (.addr(register_1_q), .data(Block), .sel(1'b1));
  Adder adder_1 (.a(register_1_q), .b(8'h1), .out(adder_1_out));  // open: cin, cout

  // Notes on the sheet:
  //   contents of rom_1 (hex, n*v repeats v):
  //   6118d88 eb970303
endmodule

// comb
module combine (
  input  [7:0] Value_0,
  input  [7:0] Value_1,
  input  Double_Const,
  output [7:0] Value_0_2,
  output [7:0] Value_1_2
);

  wire [7:0] adder_1_out;

  Adder adder_1 (.a(Value_0), .b(Value_1), .out(adder_1_out));  // open: cin, cout
  Multiplexer #(.width(8), .enable("false")) multiplexer_1 (
    .in0(Value_0), .in1(adder_1_out), .out(Value_0_2), .sel(Double_Const));

  assign Value_1_2 = Value_1;
endmodule
